// Logisim project ex4.circ as structural Verilog: 5 circuits, main circuit RotRight
module RotRight (
  input  [15:0] INPUT0,
  input  [3:0] AMOUNT,
  output [15:0] OUTPUT0
);

  wire [15:0] t1, t2, t3, t4, t5, t6, t7, t8, t9, t10, t11, t12, t13, t14, t15;

  rot1 rot1_1 (.in_1(INPUT0), .out_2(t1));
  rot2 rot2_1 (.in_1(INPUT0), .out_2(t2));
  rot4 rot4_1 (.in_1(INPUT0), .out_2(t4));
  rot8 rot8_1 (.in_1(INPUT0), .out_2(t8));
  rot1 rot1_2 (.in_1(t2), .out_2(t3));
  rot1 rot1_3 (.in_1(t4), .out_2(t5));
  rot2 rot2_2 (.in_1(t4), .out_2(t6));
  rot1 rot1_4 (.in_1(t8), .out_2(t9));
  rot2 rot2_3 (.in_1(t8), .out_2(t10));
  rot4 rot4_2 (.in_1(t8), .out_2(t12));
  rot1 rot1_5 (.in_1(t6), .out_2(t7));
  rot1 rot1_6 (.in_1(t10), .out_2(t11));
  rot1 rot1_7 (.in_1(t12), .out_2(t13));
  rot2 rot2_4 (.in_1(t12), .out_2(t14));
  rot1 rot1_8 (.in_1(t14), .out_2(t15));
  Multiplexer #(.select(4), .width(16)) multiplexer_1 (
    .in0(INPUT0), .in1(t1), .in2(t2), .in3(t3), .in4(t4), .in5(t5), .in6(t6), .in7(t7), .in8(t8), .in9(t9),
    .in10(t10), .in11(t11), .in12(t12), .in13(t13), .in14(t14), .in15(t15), .out(OUTPUT0), .sel(AMOUNT));

  // Other names for the same wires on the sheet: t0[15:0] = INPUT0
endmodule

module rot1 (
  input  [15:0] in_1,
  output [15:0] out_2
);


  assign out_2 = {in_1[0], in_1[15:1]};
endmodule

module rot2 (
  input  [15:0] in_1,
  output [15:0] out_2
);

  wire [15:0] rot1_1_out_2;

  rot1 rot1_1 (.in_1(in_1), .out_2(rot1_1_out_2));
  rot1 rot1_2 (.in_1(rot1_1_out_2), .out_2(out_2));
endmodule

module rot4 (
  input  [15:0] in_1,
  output [15:0] out_2
);

  wire [15:0] rot2_1_out_2;

  rot2 rot2_1 (.in_1(in_1), .out_2(rot2_1_out_2));
  rot2 rot2_2 (.in_1(rot2_1_out_2), .out_2(out_2));
endmodule

module rot8 (
  input  [15:0] in_1,
  output [15:0] out_2
);

  wire [15:0] rot4_1_out_2;

  rot4 rot4_1 (.in_1(in_1), .out_2(rot4_1_out_2));
  rot4 rot4_2 (.in_1(rot4_1_out_2), .out_2(out_2));
endmodule
