// Logisim project ex2.circ as structural Verilog: 1 circuit, main circuit compute_BrUn
module compute_BrUn (
  input  [31:0] INSTRUCTION,
  output BrUn
);

  wire not_1_out;

  not not_1 (not_1_out, INSTRUCTION[14]);
  or or_1 (BrUn, INSTRUCTION[13], not_1_out);
endmodule
