// Logisim project imm-gen.circ as structural Verilog: 1 circuit, main circuit imm_gen
module imm_gen (
  input  [31:0] Instruction,
  input  [2:0] ImmSel,
  output [31:0] Immediate
);

  wire [31:0] Immediate0;
  wire [31:5] Immediate1;
  wire [31:12] Immediate2;
  wire [31:20] Immediate4;

  assign Immediate0 = {{20{Instruction[31]}}, Instruction[31:20]};  // Bit_Extender bit_extender_1
  assign Immediate1 = {{20{Instruction[31]}}, Instruction[31:25]};  // Bit_Extender bit_extender_2
  assign Immediate2 = {{19{Instruction[31]}}, Instruction[31]};  // Bit_Extender bit_extender_3
  assign Immediate4 = {{11{Instruction[31]}}, Instruction[31]};  // Bit_Extender bit_extender_4
  Multiplexer #(.select(3), .width(32)) multiplexer_1 (
    .in0(Immediate0), .in1({Immediate1, Instruction[11:7]}),
    .in2({Immediate2, Instruction[7], Instruction[30:25], Instruction[11:8], 1'b0}),
    .in3({Instruction[31:12], {12{1'b0}}}),
    .in4({Immediate4, Instruction[19:12], Instruction[20], Instruction[30:21], 1'b0}), .out(Immediate),
    .sel(ImmSel));  // open: in5, in6, in7

  // Other names for the same wires on the sheet: Immediate1[4:0] = Instruction[11:7];
  //   Immediate2[11:1] = {Instruction[7], Instruction[30:25], Instruction[11:8]};
  //   Immediate3[31:12] = Instruction[31:12];
  //   Immediate4[19:1] = {Instruction[19:12], Instruction[20], Instruction[30:21]}

  // Notes on the sheet:
  //   INPUTS to your circuit
  //   DON'T CHANGE THE LOCATIONS OF THE INPUTS AND OUTPUTS!
  //   OUTPUT from your circuit
endmodule
