// Logisim project old_regfile.circ as structural Verilog: 1 circuit, main circuit regfile
module regfile (
  input  [4:0] ReadIndex1,
  input  [4:0] ReadIndex2,
  input  [4:0] WriteIndex,
  input  [31:0] WriteData,
  input  RegWEn,
  input  clk,
  output [31:0] ra,
  output [31:0] sp,
  output [31:0] t0,
  output [31:0] t1,
  output [31:0] t2,
  output [31:0] s0,
  output [31:0] s1,
  output [31:0] a0,
  output [31:0] ReadData1,
  output [31:0] ReadData2
);

  wire demultiplexer_1_out0, demultiplexer_1_out1, demultiplexer_1_out2, demultiplexer_1_out3,
       demultiplexer_1_out4, demultiplexer_1_out5, regwe;

  // AND_Gate and_1 has open pins: in0=RegWEn, in1=1'b1, out=open
  Demultiplexer #(.select(5)) demultiplexer_1 (
    .out0(demultiplexer_1_out0), .out1(demultiplexer_1_out1), .out2(demultiplexer_1_out2),
    .out3(demultiplexer_1_out3), .out4(demultiplexer_1_out4), .out5(demultiplexer_1_out5), .in(regwe),
    .sel(WriteIndex));  // open: out6, out7, out8, out9, out10, out11, out12, out13, out14, out15, out16, out17, out18, out19, out20, out21, out22, out23, out24, out25, out26, out27, out28, out29, out30, out31
  Register #(.width(32)) register_1 (.D(WriteData), .en(demultiplexer_1_out0), .clk(clk));  // open: Q, clr
  Register #(.width(32)) register_2 (.D(WriteData), .en(demultiplexer_1_out1), .clk(clk));  // open: Q, clr
  Register #(.width(32)) register_3 (.D(WriteData), .en(demultiplexer_1_out2), .clk(clk));  // open: Q, clr
  Register #(.width(32)) register_4 (.D(WriteData), .en(demultiplexer_1_out3), .clk(clk));  // open: Q, clr
  Register #(.width(32)) register_5 (.D(WriteData), .en(demultiplexer_1_out4), .clk(clk));  // open: Q, clr
  Register #(.width(32)) register_6 (.D(WriteData), .en(demultiplexer_1_out5), .clk(clk));  // open: Q, clr
  Register #(.width(32)) register_7 (.D(WriteData), .clk(clk));  // open: en, Q, clr
  Register #(.width(32)) register_8 (.D(WriteData), .clk(clk));  // open: en, Q, clr
  Register #(.width(32)) register_9 (.D(WriteData), .clk(clk));  // open: en, Q, clr
  Register #(.width(32)) register_10 (.D(WriteData), .clk(clk));  // open: en, Q, clr
  Register #(.width(32)) register_11 (.D(WriteData), .clk(clk));  // open: en, Q, clr
  Register #(.width(32)) register_12 (.D(WriteData), .clk(clk));  // open: en, Q, clr
  Register #(.width(32)) register_13 (.D(WriteData), .clk(clk));  // open: en, Q, clr
  Register #(.width(32)) register_14 (.D(WriteData), .clk(clk));  // open: en, Q, clr
  Register #(.width(32)) register_15 (.D(WriteData), .clk(clk));  // open: en, Q, clr
  Register #(.width(32)) register_16 (.D(WriteData), .clk(clk));  // open: en, Q, clr
  Register #(.width(32)) register_17 (.D(WriteData), .clk(clk));  // open: en, Q, clr
  Register #(.width(32)) register_18 (.D(WriteData), .clk(clk));  // open: en, Q, clr
  Register #(.width(32)) register_19 (.D(WriteData), .clk(clk));  // open: en, Q, clr
  Register #(.width(32)) register_20 (.D(WriteData), .clk(clk));  // open: en, Q, clr
  Register #(.width(32)) register_21 (.D(WriteData), .clk(clk));  // open: en, Q, clr
  Register #(.width(32)) register_22 (.D(WriteData), .clk(clk));  // open: en, Q, clr
  Register #(.width(32)) register_23 (.D(WriteData), .clk(clk));  // open: en, Q, clr
  Register #(.width(32)) register_24 (.D(WriteData), .clk(clk));  // open: en, Q, clr
  Register #(.width(32)) register_25 (.D(WriteData), .clk(clk));  // open: en, Q, clr
  Register #(.width(32)) register_26 (.D(WriteData), .clk(clk));  // open: en, Q, clr
  Register #(.width(32)) register_27 (.D(WriteData), .clk(clk));  // open: en, Q, clr
  Register #(.width(32)) register_28 (.D(WriteData), .clk(clk));  // open: en, Q, clr
  Register #(.width(32)) register_29 (.D(WriteData), .clk(clk));  // open: en, Q, clr
  Register #(.width(32)) register_30 (.D(WriteData), .clk(clk));  // open: en, Q, clr
  Register #(.width(32)) register_31 (.D(WriteData), .clk(clk));  // open: en, Q, clr
  Register #(.width(32)) register_32 (.D(WriteData), .clk(clk));  // open: en, Q, clr

  // Notes on the sheet:
  //   INPUTS to your circuit
  //   DON'T CHANGE THE LOCATIONS OF THE INPUTS AND OUTPUTS!
  //   These are DEBUG/TEST outputs from your circuit.
  //   OUTPUTS from your circuit
endmodule
