// Logisim project partial-store.circ as structural Verilog: 1 circuit, main circuit partial_store
module partial_store (
  input  [31:0] Instruction,
  input  [31:0] MemAddress,
  input  [31:0] DataFromReg,
  input  MemWEn,
  output [3:0] MemWriteMask,
  output [31:0] DataToMem
);

  wire [3:0] MemWriteMask0, MemWriteMask1, multiplexer_3_out;
  wire [31:0] DataToMem0, DataToMem1;

  Multiplexer #(.select(2), .width(4)) multiplexer_1 (
    .in0(4'b0001), .in1(4'b0010), .in2(4'b0100), .in3(4'b1000), .out(MemWriteMask0), .sel(MemAddress[1:0]));
  Multiplexer #(.select(2), .width(4)) multiplexer_2 (
    .in0(4'b0011), .in2(4'b1100), .out(MemWriteMask1), .sel(MemAddress[1:0]));  // open: in1, in3
  Multiplexer #(.select(3), .width(4)) multiplexer_3 (
    .in0(MemWriteMask0), .in1(MemWriteMask1), .in2(4'b1111), .out(multiplexer_3_out), .sel(Instruction[14:12]));  // open: in3, in4, in5, in6, in7
  Multiplexer #(.width(4)) multiplexer_4 (.in0(4'b0000), .in1(multiplexer_3_out), .out(MemWriteMask), .sel(MemWEn));
  Multiplexer #(.select(2), .width(32)) multiplexer_5 (
    .in0({{24{1'b0}}, DataFromReg[7:0]}), .in1({{16{1'b0}}, DataFromReg[7:0], {8{1'b0}}}),
    .in2({{8{1'b0}}, DataFromReg[7:0], {16{1'b0}}}), .in3({DataFromReg[7:0], {24{1'b0}}}), .out(DataToMem0),
    .sel(MemAddress[1:0]));
  Multiplexer #(.select(2), .width(32)) multiplexer_6 (
    .in0({{16{1'b0}}, DataFromReg[15:0]}), .in2({DataFromReg[15:0], {16{1'b0}}}), .out(DataToMem1),
    .sel(MemAddress[1:0]));  // open: in1, in3
  Multiplexer #(.select(3), .width(32)) multiplexer_7 (
    .in0(DataToMem0), .in1(DataToMem1), .in2(DataFromReg), .out(DataToMem), .sel(Instruction[14:12]));  // open: in3, in4, in5, in6, in7

  // Other names for the same wires on the sheet: Funct3[2:0] = Instruction[14:12]; rs1[4:0] = Instruction[19:15];
  //   MemBottom2[1:0] = MemAddress[1:0]

  // Notes on the sheet:
  //   INPUTS to your circuit
  //   DON'T CHANGE THE LOCATIONS OF THE INPUTS AND OUTPUTS!
  //   OUTPUT from your circuit
endmodule
