// Logisim project right_imm-gen.circ as structural Verilog: 1 circuit, main circuit imm_gen
module imm_gen (
  input  [31:0] Instruction,
  input  [2:0] ImmSel,
  output [31:0] Immediate
);

  wire isB, isI, isJ, isS, isU;
  wire [31:0] IImm;
  wire [31:11] SImm;
  wire [31:12] BImm;
  wire [31:20] JImm;

  assign IImm = {{20{Instruction[31]}}, Instruction[31:20]};  // Bit_Extender bit_extender_1
  assign SImm = {{20{Instruction[31]}}, Instruction[31]};  // Bit_Extender bit_extender_2
  assign BImm = {{19{Instruction[31]}}, Instruction[31]};  // Bit_Extender bit_extender_3
  assign JImm = {{11{Instruction[31]}}, Instruction[31]};  // Bit_Extender bit_extender_4
  Multiplexer #(.select(3), .width(32)) multiplexer_1 (
    .in0(IImm), .in1({SImm, Instruction[30:25], Instruction[11:7]}),
    .in2({BImm, Instruction[7], Instruction[30:25], Instruction[11:8], 1'b0}),
    .in3({Instruction[31:12], {12{1'b0}}}),
    .in4({JImm, Instruction[19:12], Instruction[20], Instruction[30:21], 1'b0}), .out(Immediate), .sel(ImmSel));  // open: in5, in6, in7
  Comparator #(.width(3)) comparator_1 (.a(ImmSel), .b(3'b000), .eq(isI));  // open: gt, lt
  Comparator #(.width(3)) comparator_2 (.a(ImmSel), .b(3'b001), .eq(isS));  // open: gt, lt
  Comparator #(.width(3)) comparator_3 (.a(ImmSel), .b(3'b010), .eq(isB));  // open: gt, lt
  Comparator #(.width(3)) comparator_4 (.a(ImmSel), .b(3'b011), .eq(isU));  // open: gt, lt
  Comparator #(.width(3)) comparator_5 (.a(ImmSel), .b(3'b100), .eq(isJ));  // open: gt, lt

  // Other names for the same wires on the sheet: BImm[11:1] = {Instruction[7], Instruction[30:25], Instruction[11:8]};
  //   SImm[10:0] = {Instruction[30:25], Instruction[11:7]};
  //   JImm[19:1] = {Instruction[19:12], Instruction[20], Instruction[30:21]}; UImm[31:12] = Instruction[31:12]

  // Notes on the sheet:
  //   INPUTS to your circuit
  //   DON'T CHANGE THE LOCATIONS OF THE INPUTS AND OUTPUTS!
  //   OUTPUT from your circuit
endmodule
