// Logisim project right_partial-load.circ as structural Verilog: 1 circuit, main circuit partial_load
module partial_load (
  input  [31:0] Instruction,
  input  [31:0] MemAddress,
  input  [31:0] DataFromMem,
  output [31:0] DataToReg
);

  wire and_4_out, and_5_out, and_6_out, comparator_1_eq, comparator_2_eq, comparator_3_eq, comparator_5_eq,
       comparator_6_eq, comparator_7_eq, comparator_8_eq, comparator_9_eq, comparator_10_eq,
       comparator_11_eq, comparator_12_eq, isLb, isLb0, isLb1, isLb2, isLb3, isLh, isLh0, isLh1, isLh2,
       isLoad, isLw, isLwOut;
  wire [1:0] isLbSel, isLhSel;
  wire [7:0] multiplexer_1_out, multiplexer_2_out;
  wire [15:0] bit_extender_1_out, multiplexer_3_out;
  wire [31:0] bit_extender_2_out;

  Comparator #(.width(3)) comparator_1 (.a(Instruction[14:12]), .b(3'b000), .eq(comparator_1_eq));  // open: gt, lt
  Comparator #(.width(3)) comparator_2 (.a(Instruction[14:12]), .b(3'b001), .eq(comparator_2_eq));  // open: gt, lt
  Comparator #(.width(3)) comparator_3 (.a(Instruction[14:12]), .b(3'b010), .eq(comparator_3_eq));  // open: gt, lt
  Comparator #(.width(7)) comparator_4 (.a(Instruction[6:0]), .b(7'b0000011), .eq(isLoad));  // open: gt, lt
  and and_1 (isLb, isLoad, comparator_1_eq);
  and and_2 (isLh, isLoad, comparator_2_eq);
  and and_3 (isLw, isLoad, comparator_3_eq);
  Comparator #(.width(2)) comparator_5 (.a(MemAddress[1:0]), .b(2'b00), .eq(comparator_5_eq));  // open: gt, lt
  Comparator #(.width(2)) comparator_6 (.a(MemAddress[1:0]), .b(2'b01), .eq(comparator_6_eq));  // open: gt, lt
  Comparator #(.width(2)) comparator_7 (.a(MemAddress[1:0]), .b(2'b10), .eq(comparator_7_eq));  // open: gt, lt
  Comparator #(.width(2)) comparator_8 (.a(MemAddress[1:0]), .b(2'b11), .eq(comparator_8_eq));  // open: gt, lt
  Comparator #(.width(2)) comparator_9 (.a(MemAddress[1:0]), .b(2'b00), .eq(comparator_9_eq));  // open: gt, lt
  Comparator #(.width(2)) comparator_10 (.a(MemAddress[1:0]), .b(2'b01), .eq(comparator_10_eq));  // open: gt, lt
  Comparator #(.width(2)) comparator_11 (.a(MemAddress[1:0]), .b(2'b10), .eq(comparator_11_eq));  // open: gt, lt
  Comparator #(.width(2)) comparator_12 (.a(MemAddress[1:0]), .b(2'b00), .eq(comparator_12_eq));  // open: gt, lt
  and and_4 (and_4_out, isLb, comparator_5_eq);
  and and_5 (and_5_out, isLb, comparator_6_eq);
  and and_6 (and_6_out, isLb, comparator_7_eq);
  and and_7 (isLb3, isLb, comparator_8_eq);
  and and_8 (isLh0, isLh, comparator_9_eq);
  and and_9 (isLh1, isLh, comparator_10_eq);
  and and_10 (isLh2, isLh, comparator_11_eq);
  and and_11 (isLwOut, isLw, comparator_12_eq);
  or or_1 (isLb0, isLh0, and_4_out);
  or or_2 (isLb1, isLh1, and_5_out);
  or or_3 (isLb2, isLh2, and_6_out);
  Priority_Encoder #(.select_enc(2)) priority_encoder_1 (
    .in0(isLb0), .in1(isLb1), .in2(isLb2), .in3(isLb3), .out(isLbSel));  // open: gs, en_out, en_in
  Priority_Encoder #(.select_enc(2)) priority_encoder_2 (
    .in0(isLh0), .in1(isLh1), .in2(isLh2), .out(isLhSel));  // open: in3, gs, en_out, en_in
  Multiplexer #(.select(2), .width(8)) multiplexer_1 (
    .in0(DataFromMem[7:0]), .in1(DataFromMem[15:8]), .in2(DataFromMem[23:16]), .in3(DataFromMem[31:24]),
    .out(multiplexer_1_out), .sel(isLbSel));
  assign bit_extender_1_out = {{8{multiplexer_1_out[7]}}, multiplexer_1_out};  // Bit_Extender bit_extender_1
  Multiplexer #(.select(2), .width(8)) multiplexer_2 (
    .in0(DataFromMem[15:8]), .in1(DataFromMem[23:16]), .in2(DataFromMem[31:24]), .out(multiplexer_2_out),
    .sel(isLhSel));  // open: in3
  Multiplexer #(.width(16)) multiplexer_3 (
    .in0(bit_extender_1_out), .in1({multiplexer_2_out, multiplexer_1_out}), .out(multiplexer_3_out),
    .sel(isLh));
  assign bit_extender_2_out = {{16{multiplexer_3_out[15]}}, multiplexer_3_out};  // Bit_Extender bit_extender_2
  Multiplexer #(.width(32)) multiplexer_4 (.in0(bit_extender_2_out), .in1(DataFromMem), .out(DataToReg), .sel(isLw));

  // Other names for the same wires on the sheet: Mem0[7:0] = DataFromMem[7:0]; Mem1[7:0] = DataFromMem[15:8];
  //   Mem2[7:0] = DataFromMem[23:16]; Mem3[7:0] = DataFromMem[31:24]; opcode[6:0] = Instruction[6:0];
  //   funct3[2:0] = Instruction[14:12]; bottom2bits[1:0] = MemAddress[1:0]

  // Notes on the sheet:
  //   INPUTS to your circuit
  //   DON'T CHANGE THE LOCATIONS OF THE INPUTS AND OUTPUTS!
  //   OUTPUT from your circuit
endmodule
